# Fritzing sketch 3 en 1 (saved by Fritzing 0.9.5d)
breadboards: 1

parts:
  S1 = Pushbutton [package="[SMD]"]
  S2 = Pushbutton [package="[SMD]"]
  R1 = Resistor [tolerance=±5% resistance=1k package="0603 [SMD]"]
  R2 = Resistor [tolerance=±5% resistance=1k package="0603 [SMD]"]
  R3 = Resistor [tolerance=±5% resistance=1k package="0603 [SMD]"]
  R4 = Resistor [tolerance=±5% resistance=1k package="0603 [SMD]"]
  R5 = Resistor [tolerance=±5% resistance=1k package="0603 [SMD]"]
  R6 = Resistor [tolerance=±5% resistance=1k package="0603 [SMD]"]
  R7 = Resistor [tolerance=±5% resistance=1k package="0603 [SMD]"]
  R8 = Resistor [tolerance=±5% resistance=1k package="0603 [SMD]"]
  LED2 = RGB LED (com. cathode, rgb) [package="5 mm [THT]"]
  R9 = Resistor [tolerance=±5% resistance=1k package="0603 [SMD]"]
  R10 = Resistor [tolerance=±5% resistance=1k package="0603 [SMD]"]
  R11 = Resistor [tolerance=±5% resistance=1k package="0603 [SMD]"]
  R13 = Resistor [tolerance=±5% resistance=1k package="0603 [SMD]"]
  LED3 = smd LED [color="Red (633nm)" package="1206 [SMD]"]
  LED4 = smd LED [color="Red (633nm)" package="1206 [SMD]"]
  LED5 = smd LED [color="Red (633nm)" package="1206 [SMD]"]
  LED6 = smd LED [color="Red (633nm)" package="1206 [SMD]"]
  LED7 = smd LED [color="Red (633nm)" package="1206 [SMD]"]
  LED8 = smd LED [color="Red (633nm)" package="1206 [SMD]"]
  LED9 = smd LED [color="Red (633nm)" package="1206 [SMD]"]
  LED10 = smd LED [color="Red (633nm)" package="1206 [SMD]"]
  R12 = Resistor [tolerance=±5% resistance=1k package="0603 [SMD]"]
  U2 = STM32F40x [package="LQFP64, 10x10mm"]

nets:
  N1: S1.Pin_1, S1.Pin_2, R12.Pin_0, U2.PE5
  GND: S1.Pin_3, S1.Pin_4, S2.Pin_3, S2.Pin_4, R1.Pin_1, R2.Pin_1, R3.Pin_1, R4.Pin_1, R5.Pin_1, R6.Pin_1, R7.Pin_1, R8.Pin_1, LED2.common_cathode, U2.VDD4
  N2: S2.Pin_1, S2.Pin_2, R13.Pin_0, U2.PE4
  N3: R1.Pin_0, LED10.cathode
  N4: R2.Pin_0, LED5.cathode
  N5: R3.Pin_0, LED6.cathode
  N6: R4.Pin_0, LED7.cathode
  N7: R5.Pin_0, LED8.cathode
  N8: R6.Pin_0, LED9.cathode
  N9: R7.Pin_0, LED4.cathode
  N10: R8.Pin_0, LED3.cathode
  N11: LED2.red_anode, R9.Pin_1
  N12: LED2.green_anode, R10.Pin_1
  N13: LED2.blue_anode, R11.Pin_1
  N14: R9.Pin_0, U2.PD14
  N15: R10.Pin_0, U2.PD12
  N16: R11.Pin_0, U2.PD15
  N17: R13.Pin_1, R12.Pin_1, U2.V5
  N18: LED3.anode, U2.PD7
  N19: LED4.anode, U2.PD6
  N20: LED5.anode, U2.PD1
  N21: LED6.anode, U2.PD2
  N22: LED7.anode, U2.PD3
  N23: LED8.anode, U2.PD4
  N24: LED9.anode, U2.PD5
  N25: LED10.anode, U2.PD0

custom parts:
  STM32F40x: STM32F405xx and STM32F407xx microcontroller in LQFP64 pinout. ARM Cortex-M4 32b MCU+FPU
