# Fritzing sketch TecladoaDisplay (saved by Fritzing 0.9.5d)
breadboards: 2

parts:
  LED1 = 7-SEGMENT-4DIGIT-YOUNGSUN [package=7-segment-4digit-youngsun-longpads]
  LED2 = 7-SEGMENT-4DIGIT-YOUNGSUN [package=7-segment-4digit-youngsun]
  IC1 = IC, DIP package, 16 pins [chip_label=74LS47]
  IC2 = IC, DIP package, 16 pins [chip_label=74HC238]
  R1 = Resistor [tolerance=±5% resistance=1k package="2512 [SMD]"]
  R2 = Resistor [tolerance=±5% resistance=1k package="2512 [SMD]"]
  R3 = Resistor [tolerance=±5% resistance=1k package="2512 [SMD]"]
  R4 = Resistor [tolerance=±5% resistance=1k package="2512 [SMD]"]
  R5 = Resistor [tolerance=±5% resistance=1k package="2512 [SMD]"]
  R6 = Resistor [tolerance=±5% resistance=1k package="2512 [SMD]"]
  R7 = Resistor [tolerance=±5% resistance=1k package="2512 [SMD]"]
  U1 = STM32F40x [package="LQFP64, 10x10mm"]
  S1 = Pushbutton [package="[SMD]"]
  R8 = Resistor [tolerance=±5% resistance=1k package="2512 [SMD]"]
  Matrix_keypad1 = KEYPAD 4x4

nets:
  N1: LED1.DIG1, IC2.pin15
  N2: LED1.DIG2, IC2.pin14
  N3: LED1.D, LED2.D, R5.Pin_0
  N4: LED1.E, LED2.E, R4.Pin_0
  N5: LED1.DIG3, IC2.pin13
  N6: LED1.DIG4, IC2.pin12
  N7: LED1.F, LED2.F, R1.Pin_0
  N8: LED1.C, LED2.C, R6.Pin_0
  N9: LED1.A, LED2.A, R3.Pin_0
  N10: LED1.G, LED2.G, R2.Pin_0
  N11: LED1.B, LED2.B, R7.Pin_0
  N12: LED2.DIG1, IC2.pin11
  N13: LED2.DIG2, IC2.pin10
  N14: LED2.DIG3, IC2.pin9
  N15: LED2.DIG4, IC2.pin7
  N16: IC1.pin1, U1.PC1
  N17: IC1.pin2, U1.PD0
  N18: IC1.pin6, U1.PD1
  N19: IC1.pin7, U1.PC0
  N20: IC1.pin8, IC2.pin4, IC2.pin5, IC2.pin8, U1.VDD4, S1.Pin_3, S1.Pin_4
  N21: IC1.pin9, R4.Pin_1
  N22: IC1.pin10, R5.Pin_1
  N23: IC1.pin11, R6.Pin_1
  N24: IC1.pin12, R7.Pin_1
  N25: IC1.pin13, R3.Pin_1
  N26: IC1.pin14, R2.Pin_1
  N27: IC1.pin15, R1.Pin_1
  N28: IC1.pin16, IC2.pin6, IC2.pin16, U1.V5, R8.Pin_1
  N29: IC2.pin1, U1.PD2
  N30: IC2.pin2, U1.PD3
  N31: IC2.pin3, U1.PD4
  N32: U1.PD5, S1.Pin_1, S1.Pin_2, R8.Pin_0
  N33: U1.PA10, Matrix_keypad1.col1
  N34: U1.PA11, Matrix_keypad1.col2
  N35: U1.PA12, Matrix_keypad1.col3
  N36: U1.PA13, Matrix_keypad1.col4
  N37: U1.PA15, Matrix_keypad1.row1
  N38: U1.PC10, Matrix_keypad1.row2
  N39: U1.PC11, Matrix_keypad1.row3
  N40: U1.PC12, Matrix_keypad1.row4

custom parts:
  STM32F40x: STM32F405xx and STM32F407xx microcontroller in LQFP64 pinout. ARM Cortex-M4 32b MCU+FPU
  KEYPAD 4x4: Matrix keypad 16 buttons, 4 rows x 4 columns
