# Fritzing sketch ADCtoPWM (saved by Fritzing 0.9.5d)
breadboards: 1

parts:
  U1 = STM32F40x [package="LQFP64, 10x10mm"]
  R1 = Trimmer Potentiometer [maximum_resistance=5kΩ package=THT]
  LED1 = LED - 5mm [color="Red (633nm)" package="5 mm [THT]"]
  R2 = Resistor [tolerance=±5% resistance=220 package=THT]

nets:
  N1: U1.V5, R1.leg1, R2.Pin_0
  N2: U1.PB0, R1.wiper
  N3: U1.PC11, LED1.anode
  N4: U1.VDD4, R1.leg2
  N5: LED1.cathode, R2.Pin_1

custom parts:
  STM32F40x: STM32F405xx and STM32F407xx microcontroller in LQFP64 pinout. ARM Cortex-M4 32b MCU+FPU
