# Fritzing sketch ADCtoRGB (saved by Fritzing 0.9.5d)
breadboards: 1

parts:
  U1 = STM32F40x [package="LQFP64, 10x10mm"]
  LED1 = RGB LED (com. cathode, rgb) [package="5 mm [THT]"]
  R1 = Trimmer Potentiometer [maximum_resistance=5kΩ package=THT]

nets:
  N1: U1.V5, R1.leg1
  N2: U1.PD12, LED1.green_anode
  N3: U1.PD14, LED1.red_anode
  N4: U1.PD15, LED1.blue_anode
  N5: U1.PB0, R1.wiper
  N6: U1.VDD4, LED1.common_cathode, R1.leg2

custom parts:
  STM32F40x: STM32F405xx and STM32F407xx microcontroller in LQFP64 pinout. ARM Cortex-M4 32b MCU+FPU
