# Fritzing sketch IN_OUT (saved by Fritzing 0.9.5d)
breadboards: 1

parts:
  R1 = Resistor [tolerance=±5% resistance=1k package="0603 [SMD]"]
  R2 = Resistor [tolerance=±5% resistance=1k package="0603 [SMD]"]
  R3 = Resistor [tolerance=±5% resistance=1k package="0603 [SMD]"]
  R4 = Resistor [tolerance=±5% resistance=1k package="0603 [SMD]"]
  R5 = Resistor [tolerance=±5% resistance=1k package="0603 [SMD]"]
  R6 = Resistor [tolerance=±5% resistance=1k package="0603 [SMD]"]
  R7 = Resistor [tolerance=±5% resistance=1k package="0603 [SMD]"]
  R8 = Resistor [tolerance=±5% resistance=1k package="0603 [SMD]"]
  LED3 = smd LED [color="Red (633nm)" package="1206 [SMD]"]
  LED4 = smd LED [color="Red (633nm)" package="1206 [SMD]"]
  LED5 = smd LED [color="Red (633nm)" package="1206 [SMD]"]
  LED6 = smd LED [color="Red (633nm)" package="1206 [SMD]"]
  LED7 = smd LED [color="Red (633nm)" package="1206 [SMD]"]
  LED8 = smd LED [color="Red (633nm)" package="1206 [SMD]"]
  LED9 = smd LED [color="Red (633nm)" package="1206 [SMD]"]
  LED10 = smd LED [color="Red (633nm)" package="1206 [SMD]"]
  R12 = Resistor [tolerance=±5% resistance=1k package="0603 [SMD]"]
  U2 = STM32F40x [package="LQFP64, 10x10mm"]
  SW1 = DIP Switch 8 Position [package=dipswitch-08]
  R13 = Resistor [tolerance=±5% resistance=1k package="0603 [SMD]"]
  R14 = Resistor [tolerance=±5% resistance=1k package="0603 [SMD]"]
  R15 = Resistor [tolerance=±5% resistance=1k package="0603 [SMD]"]
  R16 = Resistor [tolerance=±5% resistance=1k package="0603 [SMD]"]
  R17 = Resistor [tolerance=±5% resistance=1k package="0603 [SMD]"]
  R18 = Resistor [tolerance=±5% resistance=1k package="0603 [SMD]"]
  R19 = Resistor [tolerance=±5% resistance=1k package="0603 [SMD]"]

nets:
  N1: R1.Pin_0, LED10.cathode
  GND: R1.Pin_1, R2.Pin_1, R3.Pin_1, R4.Pin_1, R5.Pin_1, R6.Pin_1, R7.Pin_1, R8.Pin_1, U2.VDD4, SW1.9, SW1.10, SW1.11, SW1.12, SW1.13, SW1.14, SW1.15, SW1.16
  N2: R2.Pin_0, LED5.cathode
  N3: R3.Pin_0, LED6.cathode
  N4: R4.Pin_0, LED7.cathode
  N5: R5.Pin_0, LED8.cathode
  N6: R6.Pin_0, LED9.cathode
  N7: R7.Pin_0, LED4.cathode
  N8: R8.Pin_0, LED3.cathode
  N9: LED3.anode, U2.PD7
  N10: LED4.anode, U2.PD6
  N11: LED5.anode, U2.PD1
  N12: LED6.anode, U2.PD2
  N13: LED7.anode, U2.PD3
  N14: LED8.anode, U2.PD4
  N15: LED9.anode, U2.PD5
  N16: LED10.anode, U2.PD0
  N17: R12.Pin_0, U2.PA10, SW1.8
  N18: R12.Pin_1, U2.V5, R13.Pin_1, R14.Pin_1, R15.Pin_1, R16.Pin_1, R17.Pin_1, R18.Pin_1, R19.Pin_1
  N19: U2.PA11, SW1.7, R13.Pin_0
  N20: U2.PA12, SW1.6, R14.Pin_0
  N21: U2.PA13, SW1.5, R15.Pin_0
  N22: U2.VCAP2, SW1.4, R16.Pin_0
  N23: U2.VDD3, SW1.3, R17.Pin_0
  N24: U2.PA14, SW1.2, R18.Pin_0
  N25: U2.PA15, SW1.1, R19.Pin_0

custom parts:
  STM32F40x: STM32F405xx and STM32F407xx microcontroller in LQFP64 pinout. ARM Cortex-M4 32b MCU+FPU
