# Fritzing sketch RampaPWM (saved by Fritzing 0.9.5d)
breadboards: 1

parts:
  U1 = STM32F40x [package="LQFP64, 10x10mm"]
  LED1 = LED - 5mm [color="Red (633nm)" package="5 mm [THT]"]
  R2 = Resistor [tolerance=±5% resistance=220 package=THT]

nets:
  N1: U1.V5, R2.Pin_0
  N2: U1.PC11, LED1.anode
  N3: LED1.cathode, R2.Pin_1

custom parts:
  STM32F40x: STM32F405xx and STM32F407xx microcontroller in LQFP64 pinout. ARM Cortex-M4 32b MCU+FPU
