# Fritzing sketch RGBCounter (saved by Fritzing 0.9.5d)
breadboards: 1

parts:
  LED2 = RGB LED (com. cathode, rgb) [package="5 mm [THT]"]
  R9 = Resistor [tolerance=±5% resistance=1k package="0603 [SMD]"]
  R10 = Resistor [tolerance=±5% resistance=1k package="0603 [SMD]"]
  R11 = Resistor [tolerance=±5% resistance=1k package="0603 [SMD]"]
  U2 = STM32F40x [package="LQFP64, 10x10mm"]

nets:
  N1: LED2.red_anode, R9.Pin_1
  N2: LED2.common_cathode, U2.VDD4
  N3: LED2.green_anode, R10.Pin_1
  N4: LED2.blue_anode, R11.Pin_1
  N5: R9.Pin_0, U2.PD14
  N6: R10.Pin_0, U2.PD12
  N7: R11.Pin_0, U2.PD15

custom parts:
  STM32F40x: STM32F405xx and STM32F407xx microcontroller in LQFP64 pinout. ARM Cortex-M4 32b MCU+FPU
